// Logisim project 7seg.circ as structural Verilog: 1 circuit, main circuit main
module main (
);

  wire and_1_out, and_2_out, and_3_out, and_4_out, and_5_out, clock_1_out, clock_2_out, clock_3_out,
       clock_4_out, nand_1_out, nand_2_out, nand_3_out, nand_4_out, nor_1_out, not_1_out, not_2_out,
       not_3_out, not_4_out, not_5_out, not_6_out, not_7_out, not_8_out, not_9_out, or_1_out, or_2_out,
       or_3_out, or_4_out, or_5_out, or_6_out, xnor_1_out, xor_1_out, xor_2_out, xor_3_out, xor_4_out,
       xor_5_out;

  Clock #(.highDuration(8), .lowDuration(8)) clock_1 (.out(clock_1_out));
  Clock #(.highDuration(4), .lowDuration(4)) clock_2 (.out(clock_2_out));
  and and_1 (and_1_out, not_2_out, clock_3_out, not_1_out);
  not not_1 (not_1_out, clock_1_out);
  not not_2 (not_2_out, clock_4_out);
  Clock #(.highDuration(2), .lowDuration(2)) clock_3 (.out(clock_3_out));
  Clock clock_4 (.out(clock_4_out));
  xnor xnor_1 (xnor_1_out, clock_2_out, clock_4_out);
  or or_1 (or_1_out, and_1_out, and_2_out);
  and and_2 (and_2_out, not_2_out, not_3_out, not_4_out);
  not not_3 (not_3_out, clock_3_out);
  not not_4 (not_4_out, clock_2_out);
  or or_2 (or_2_out, clock_1_out, clock_3_out);
  or or_3 (or_3_out, xnor_1_out, or_2_out);
  LED led_1 (.in(or_3_out));
  LED led_2 (.in(or_3_out));
  LED led_3 (.in(or_3_out));
  LED led_4 (.in(or_5_out));
  LED led_5 (.in(or_5_out));
  LED led_6 (.in(and_5_out));
  LED led_7 (.in(and_5_out));
  LED led_8 (.in(or_1_out));
  LED led_9 (.in(or_1_out));
  LED led_10 (.in(nand_1_out));
  LED led_11 (.in(nand_1_out));
  LED led_12 (.in(nand_1_out));
  nand nand_1 (nand_1_out, not_5_out, and_3_out);
  and and_3 (and_3_out, or_4_out, xor_2_out);
  not not_5 (not_5_out, clock_1_out);
  or or_4 (or_4_out, clock_4_out, not_8_out);
  xor xor_1 (xor_1_out, clock_3_out, clock_4_out);
  and and_4 (and_4_out, xor_1_out, xor_3_out);
  or or_5 (or_5_out, and_4_out, nor_1_out);
  nand nand_2 (nand_2_out, xor_4_out, clock_2_out);
  LED led_13 (.in(nand_2_out));
  LED led_14 (.in(nand_2_out));
  LED led_15 (.in(nand_3_out));
  LED led_16 (.in(nand_3_out));
  xor xor_2 (xor_2_out, xor_5_out, clock_2_out);
  xor xor_3 (xor_3_out, clock_1_out, clock_2_out);
  nor nor_1 (nor_1_out, clock_4_out, clock_3_out);
  and and_5 (and_5_out, nand_4_out, or_6_out);
  not not_6 (not_6_out, clock_4_out);
  nand nand_3 (nand_3_out, not_6_out, clock_3_out, not_9_out, not_7_out);
  not not_7 (not_7_out, clock_1_out);
  not not_8 (not_8_out, clock_3_out);
  xor xor_4 (xor_4_out, clock_4_out, clock_3_out);
  nand nand_4 (nand_4_out, clock_4_out, clock_3_out, clock_2_out);
  or or_6 (or_6_out, clock_3_out, clock_2_out, clock_1_out);
  not not_9 (not_9_out, clock_2_out);
  xor xor_5 (xor_5_out, clock_3_out, clock_4_out);

  // Notes on the sheet:
  //   D   C   B   A
endmodule
